# Fritzing sketch Hedgehog_V1 (saved by Fritzing 0.9.2b)

parts:
  Part1 = Arduino MKR WiFi 1010
  TFT1 = 1.44" SPI TFT Graphics Display 128x128 [package=THT]
  Part2 = Adafruit VL530X Time of Flight Distance Sensor [part_number="Adafruit #3317"]
  KY-1 = Keyes Relay [package=THT]
  IR2 = TSOP312.., 314.. [package=THT]
  LED2 = LED - 3mm [color="Infrared (940nm)" package="3 mm [THT]"]
  J1 = Basic Servo
  LLC1 = Logic Level Converter [package="Breakout board"]
  R1 = Resistor [tolerance=±5% resistance=220 package="2512 [SMD]"]
  R2 = Resistor [tolerance=±5% resistance=220 package="2512 [SMD]"]
  DS1 = DS18B20 1-Wire Temperature Sensor [part_number=DS18B20]

nets:
  N1: Part1.D0, DS1.DQ
  N2: Part1.D1, R2.Pin_0
  N3: Part1.D2_PWM, LLC1.LV1
  N4: Part1.D3_PWM, LLC1.LV2
  N5: Part1.D4_PWM, LLC1.LV3
  N6: Part1.D5_PWM, TFT1.pin11
  N7: Part1.D6, TFT1.pin10
  N8: Part1.D7, TFT1.pin9
  N9: Part1.D8_MOSI, TFT1.pin8
  N10: Part1.D9_SCK, TFT1.pin7
  N11: Part1.D11_SDA, Part2.SDA
  N12: Part1.D12_SCL, Part2.SCL
  VCC: Part1.VCC, Part2.VCC, LLC1.LV
  5V: Part1.5V, J1.vcc
  N13: TFT1.pin3, Part2.GND
  N14: KY-1.signal, LLC1.HV1
  N15: KY-1.ground, IR2.GND, LLC1.H-GND
  N16: IR2.Vs, R1.Pin_1
  N17: IR2.Data, LLC1.HV2
  N18: LED2.anode, R2.Pin_1
  N19: J1.pulse, LLC1.HV3

notes:
  VL53L1X TOF
  LCD Screen 1.44"
  220V Relay
  IR Sensor TSOPXXXX
  IR LED
  DS18B20 Temperature
  3.3V to 5V step up
  Arduino MKR 1010
  Servo Motor SG90

custom parts:
  Arduino MKR WiFi 1010: This is the newest version of the MKR 1000 WIFI, but with an ESP32 module on board made by U-BLOX.
  1.44" SPI TFT Graphics Display 128x128: This is for https://www.amazon.com/gp/product/B07B4BDWCL/ref=ask_ql_qh_dp_hza display. Note that this display is sold with a misprinted silkscreen indicating I2C connections on P2 connector, it is actualy SPI. The P1 connections are non functional on this board from the linked URL seller on Amazon.
  Adafruit VL530X Time of Flight Distance Sensor: The VL53L0X is a Time of Flight distance sensor like no other you've used! The sensor contains a very tiny invisible laser source, and a matching sensor. The VL53L0X can detect the "time of flight", or how long the light has taken to bounce back to the sensor. Since it uses a very narrow light source, it is good for determining distance of only the surface directly in front of it. Unlike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
  Keyes Relay: The Keyes 5V relay module is suitable for SCM development, home appliance control. It uses a 5V~12V TIL control signal which can control DC / AC signal.
  Logic Level Converter: 5V to/from 3.3V logic level converter
